# Fritzing sketch remote (saved by Fritzing 0.9.4)
breadboards: 1

parts:
  SERVO1 = Tower Pro SG90 servo [part_number=101246]
  U1 = ESP32-38PinWide [part_number=ESP32-38PinWide]
  GY1 = GY-521 (MPU-6050) [form="♀ (female)" package=THT]
  U2 = V_REG_LD1117VXX [package=78xxl]
  U3 = LIPO-600mAh [package=lipo-600]

nets:
  N1: SERVO1.Signal, U1.GPIO4
  N2: SERVO1.+5V, U1.3.3, GY1.pin1, U2.OUT
  GND: SERVO1.GND, U1.GND, GY1.pin2, U2.GND, U3.-
  N3: U1.GPIO21, GY1.pin4
  N4: U1.GPIO22, GY1.pin3
  N5: U2.IN, U3.+

custom parts:
  Tower Pro SG90 servo: Original file by John De Cristofaro http://www.adafruit.com/products/1449 Adafruit Feedback Servo (Small) Edited by: e-radionica.com 28/9/2015
  ESP32-38PinWide: Generic 38-Pin ESP32 with wide format (only access to one side of pins on a breadboard) based on Stephen Lilley's HiLetgo ESP-WROOM-32 ESP32 ESP-32S Development Board.
  GY-521 (MPU-6050): Placa GY-521 basada en conjunto de acelerómetro+giroscopios MPU-6050
  V_REG_LD1117VXX: LD1117VXX voltage regulator. We carry the 3.3V version (COM-00526) in TO-220 package.
  LIPO-600mAh: 600mAh Lipo-battery
